# Fritzing sketch Hugin_Joystick (saved by Fritzing 0.8.7b)
circuit board: 4.85897cm x 2.6006cm
breadboards: 1

parts:
  J1 = female pin header, 3 pins [form="♀ (female)"]
  1K2 = Resistor [tolerance=±5% resistance=1.2k package=THT]
  U1 = mystery part, 24 pins [chip_label="Pro Micro"]
  Q1 = NPN-Transistor [package="TO92 [THT]"]
  1K2_2 = Resistor [tolerance=±5% resistance=1.2k package=THT]

nets:
  N1: J1.pin1, U1.pin4, Q1.E
  N2: J1.pin2, 1K2.Pin_1, U1.pin21
  N3: J1.pin3, 1K2_2.Pin_1
  N4: 1K2.Pin_0, U1.pin2, Q1.C
  N5: Q1.B, 1K2_2.Pin_0

notes:
  HUGIN JOYSTICK
  NPN
  S + -
