# Fritzing sketch Hugin_PCB (saved by Fritzing 0.9.2b)
circuit board: 7.18858cm x 5.49526cm
breadboards: 1

parts:
  BeagleBone1 = BeagleBone Black  # not connected
  ATMega328 = atmega328 [package=dip]
  C2 = Ceramic Capacitor [capacitance=100nF package="200 mil [THT, multilayer]"]
  C3 = Ceramic Capacitor [capacitance=100nF package="200 mil [THT, multilayer]"]
  L_LVL_CNVRT = Logic Level Converter
  S_Bus_5V_GND = male pin header, 3 pins [form="♂ (male)"]
  SCL_SDA = male pin header, 2 pins [form="♂ (male)"]
  5V = male pin header, 4 pins [form="♂ (male)"]
  PWM_IN_4321 = male pin header, 4 pins [form="♂ (male)"]
  GND = male pin header, 4 pins [form="♂ (male)"]
  5V_2 = male pin header, 4 pins [form="♂ (male)"]
  PWM_OUT_1234 = male pin header, 4 pins [form="♂ (male)"]
  GND_2 = male pin header, 4 pins [form="♂ (male)"]
  GND_3V3_5V_(BBB) = male pin header, 3 pins [form="♂ (male)"]
  GND_3 = male pin header, 3 pins [form="♂ (male)"]
  Cape1 = male pin header, 3 pins [form="♂ (male)"]
  Cape6 = male pin header, 3 pins [form="♂ (male)"]  # not connected
  16_MHz = Crystal [frequency="16 Mhz" package=THT]
  R2_1kΩ_INV = Resistor [tolerance=±5% resistance=1k package=THT]
  R1_10kΩ_RST = Resistor [tolerance=±5% resistance=10k package=THT]
  FreeIMU = FreeIMU [package="DIP (Dual Inline) [THT]"]
  GND_5V_D12_Spare = male pin header, 3 pins [form="♂ (male)"]
  R4_220Ω_LED = Resistor [tolerance=±5% resistance=220 package=THT]
  R5_220Ω_LED = Resistor [tolerance=±5% resistance=220 package=THT]
  LED_(Atmega) = LED - 5mm [color="Red (633nm)" package="5 mm [THT]"]
  LED_(BBB) = LED - 5mm [color="Red (633nm)" package="5 mm [THT]"]
  BBB_LED = male pin header, 2 pins [form="♂ (male)"]
  Q1_INV = NPN-Transistor [package="TO92 [THT]"]
  Cape2 = male pin header, 23 pins [form="♂ (male)"]  # not connected
  Cape3 = male pin header, 23 pins [form="♂ (male)"]  # not connected
  R3_1kΩ_INV = Resistor [tolerance=±5% resistance=1k package=THT]
  SDA_SCL_5V_GND_Spare = male pin header, 4 pins [form="♂ (male)"]
  A0_5V_GND_Spare = male pin header, 3 pins [form="♂ (male)"]

nets:
  N1: ATMega328.RESET, R1_10kΩ_RST.Pin_1
  N2: ATMega328.D0_(RX), Q1_INV.E, R3_1kΩ_INV.Pin_1
  N3: ATMega328.D2, PWM_IN_4321.pin1
  N4: ATMega328.D3_(PWM), PWM_IN_4321.pin2
  N5: ATMega328.D4, PWM_IN_4321.pin3
  VCC: ATMega328.VCC, ATMega328.AVCC, L_LVL_CNVRT.HV, S_Bus_5V_GND.pin2, 5V.pin1, 5V.pin2, 5V.pin3, 5V.pin4, 5V_2.pin1, 5V_2.pin2, 5V_2.pin3, 5V_2.pin4, GND_3V3_5V_(BBB).pin3, R1_10kΩ_RST.Pin_0, FreeIMU.VIN, GND_5V_D12_Spare.pin2, R3_1kΩ_INV.Pin_0, SDA_SCL_5V_GND_Spare.pin3, A0_5V_GND_Spare.pin2
  GND: ATMega328.GND, C2.0, C3.1, L_LVL_CNVRT.GND, S_Bus_5V_GND.pin3, GND.pin1, GND.pin2, GND.pin3, GND.pin4, GND_2.pin1, GND_2.pin2, GND_2.pin3, GND_2.pin4, GND_3V3_5V_(BBB).pin1, GND_3.pin2, GND_3.pin3, Cape1.pin2, Cape1.pin3, FreeIMU.GND, GND_5V_D12_Spare.pin1, LED_(Atmega).anode, LED_(BBB).anode, Q1_INV.C, SDA_SCL_5V_GND_Spare.pin4, A0_5V_GND_Spare.pin1
  N6: ATMega328.XLAT1, C3.0, 16_MHz.pin_1
  N7: ATMega328.XLAT2, C2.1, 16_MHz.pin_0
  N8: ATMega328.D5_(PWM), PWM_IN_4321.pin4
  N9: ATMega328.D6_(PWM), PWM_OUT_1234.pin4
  N10: ATMega328.D9_(PWM), PWM_OUT_1234.pin3
  N11: ATMega328.D10_(PWM), PWM_OUT_1234.pin2
  N12: ATMega328.D11_(PWM), PWM_OUT_1234.pin1
  N13: ATMega328.D12, GND_5V_D12_Spare.pin3
  N14: ATMega328.D13, R4_220Ω_LED.Pin_1
  N15: ATMega328.A0, A0_5V_GND_Spare.pin3
  N16: ATMega328.A4, SCL_SDA.pin1, FreeIMU.SDA, SDA_SCL_5V_GND_Spare.pin1
  N17: ATMega328.A5, SCL_SDA.pin2, FreeIMU.SCL, SDA_SCL_5V_GND_Spare.pin2
  N18: L_LVL_CNVRT.TX2_LV, S_Bus_5V_GND.pin1
  N19: L_LVL_CNVRT.LV, GND_3V3_5V_(BBB).pin2, FreeIMU.3V3
  N20: L_LVL_CNVRT.TX2_HV, R2_1kΩ_INV.Pin_0
  N21: R2_1kΩ_INV.Pin_1, Q1_INV.B
  N22: R4_220Ω_LED.Pin_0, LED_(Atmega).cathode
  N23: R5_220Ω_LED.Pin_0, BBB_LED.pin1
  N24: R5_220Ω_LED.Pin_1, LED_(BBB).cathode

notes:
  S.Bus in
  S.Bus out
  Spare
  I2C
  PWM in
  PWM out
  Power options:
  5V, 1A to barrel plug on BBB (positive in the middle of the barrel plug). 3rd line (Expansion header, PIN 5-6) will provide power if BBB is powered from the barrel plug.
  Power BBB via 3rd line (Expansion header, PIN 5-6), 5V +/- 0.25V. This is used on Hugin. 5V from RC receiver, PWM in, PWM out.
  Inputs to FreeIMU part incorrect

custom parts:
  BeagleBone Black: BeagleBone Black rev. A5B
