# Fritzing sketch Hugin_Protoboard (saved by Fritzing 0.9.2b)
breadboards: 1

parts:
  U1 = mystery part, 8 pins [chip_label=FreeIMUv04]
  U2 = mystery part, 8 pins [chip_label=Receiver]
  Part1 = Logic Level Converter
  Q1 = NPN-Transistor [package="TO92 [THT]"]
  S_Bus = female pin header, 3 pins [form="♀ (female)"]
  R1 = Resistor [tolerance=±5% resistance=1.2k package=THT]
  R2 = Resistor [tolerance=±5% resistance=2.2k package=THT]
  PWM_in = female pin header, 4 pins [form="♀ (female)"]
  Part2 = Arduino Uno (Rev3)
  BeagleBone1 = BeagleBone Black
  U3 = mystery part, 10 pins [chip_label="COTS Controller"]
  U4 = mystery part, 4 pins [chip_label=QBrain]
  PWM_out = female pin header, 4 pins [form="♀ (female)"]

nets:
  N1: U1.pin4, Part2.A5/SCL, BeagleBone1.no_name_yet#19
  N2: U1.pin5, Part2.A4/SDA, BeagleBone1.no_name_yet#20
  N3: U1.pin6, Part1.LV, Part2.3V3
  GND: U1.pin7, U2.pin8, Part1.GND, Q1.E, S_Bus.pin3, Part2.GND, BeagleBone1.no_name_yet#1, BeagleBone1.no_name_yet#3
  N4: U2.pin1, U3.pin1
  N5: U2.pin2, U3.pin2
  N6: U2.pin3, U3.pin3
  N7: U2.pin4, U3.pin4
  N8: U2.pin5, U3.pin5
  N9: U2.pin6, Part1.TX_LV, S_Bus.pin1
  N10: U2.pin7, Part1.HV, S_Bus.pin2, R2.Pin_0, Part2.5V, BeagleBone1.no_name_yet#6
  N11: Part1.TX_HV, R1.Pin_0
  N12: Q1.B, R1.Pin_1
  N13: Q1.C, R2.Pin_1, Part2.D0/RX
  N14: PWM_in.pin1, Part2.D2
  N15: PWM_in.pin2, Part2.D3_PWM
  N16: PWM_in.pin3, Part2.D4
  N17: PWM_in.pin4, Part2.D5_PWM
  N18: Part2.D9_PWM, PWM_out.pin2
  N19: Part2.D10_PWM/SS, PWM_out.pin3
  N20: Part2.D11_PWM/MOSI, PWM_out.pin4
  N21: Part2.D6_PWM, PWM_out.pin1
  N22: U3.pin7, U4.pin4
  N23: U3.pin8, U4.pin3
  N24: U3.pin9, U4.pin2
  N25: U3.pin10, U4.pin1

notes:
  Inverter
  Third line is 5V from barrel plug. Fourth line is internal 5V
  PWM in
  PWM out

custom parts:
  BeagleBone Black: BeagleBone Black rev. A5B
