# Fritzing sketch Hugin_breadboard (saved by Fritzing 0.9.2b)
circuit board: 7.18858cm x 5.49526cm
breadboards: 1

parts:
  BeagleBone1 = BeagleBone Black
  U5 = mystery part, 4 pins [chip_label=QBrain]
  U9 = Mystery Part - 10 pins [chip_label=KK2.15 package=THT]
  Part1 = Arduino Uno (Rev3)
  JACK1 = 2.1mm DC Barrel Jack
  Part3 = Logic Level Converter
  S_BUS_in = male pin header, 3 pins [form="♂ (male)"]
  Q2 = NPN-Transistor [package="TO92 [THT]"]
  U11 = FreeIMU [chip_label=FreeIMU package=THT]
  Part4 = 16-Channel 12-bit PCA9685 PWM/Servo Driver
  LED_(BBB)1 = LED - 5mm [color="Green (555nm)" package="5 mm [THT]"]
  LED_(BBB)2 = LED - 5mm [color="Blue (470nm)" package="5 mm [THT]"]
  R5_220Ω_LED1 = Resistor [tolerance=±5% resistance=220 package=THT]
  R5_220Ω_LED2 = Resistor [tolerance=±5% resistance=220 package=THT]
  S1 = Pushbutton [package=THT]
  U10 = Mystery Part - 8 pins [chip_label="Receiver R7008SB" package=THT]
  R3_1kΩ_INV1 = Resistor [tolerance=±5% resistance=1k package=THT]
  R3_1kΩ_INV2 = Resistor [tolerance=±5% resistance=1k package=THT]
  J1 = Basic Servo
  J2 = Basic Servo
  J3 = Basic Servo
  J4 = Basic Servo
  J5 = female pin header, 3 pins [form="♀ (female)"]
  J6 = female pin header, 3 pins [form="♀ (female)"]
  J7 = female pin header, 3 pins [form="♀ (female)"]
  J8 = female pin header, 3 pins [form="♀ (female)"]
  R2 = Resistor [tolerance=±5% resistance=10k package=THT]
  R3 = Resistor [tolerance=±5% resistance=10k package=THT]

nets:
  GND: BeagleBone1.no_name_yet#1, Part1.GND, JACK1.switch, Part3.GND, S_BUS_in.pin3, Q2.E, U11.GND, Part4.GND, LED_(BBB)1.cathode, LED_(BBB)2.cathode, U10.6, J1.gnd, J2.gnd, J3.gnd, J4.gnd, J5.pin3, R3.Pin_1
  VCC: BeagleBone1.no_name_yet#5, Part1.VIN, JACK1.center, Part3.HV, S_BUS_in.pin2, U11.VIN, Part4.V+, Part4.VCC, U10.7/8, R3_1kΩ_INV1.Pin_1, J1.vcc, J2.vcc, J3.vcc, J4.vcc, J5.pin2, J6.pin2, J7.pin2, J8.pin2, R2.Pin_1
  N1: BeagleBone1.no_name_yet#11, R5_220Ω_LED2.Pin_1
  N2: BeagleBone1.no_name_yet#19, Part1.A5/SCL, U11.SCL, Part4.SCL
  N3: BeagleBone1.no_name_yet#20, Part1.A4/SDA, U11.SDA, Part4.SDA
  N4: BeagleBone1.no_name_yet#118, Part3.TX2_LV, S1.leg0, R3.Pin_0
  N5: U5.pin1, U9.Mo1
  N6: U5.pin2, U9.Mo2
  N7: U5.pin3, U9.Mo3
  N8: U5.pin4, U9.Mo4
  N9: U9.AIL, U10.1
  N10: U9.ELE, U10.2
  N11: U9.THR, U10.3
  N12: U9.RUDD, U10.4
  N13: U9.AUX, U10.5
  N14: Part1.D9_PWM, Part4.0, J1.pulse, J5.pin1
  N15: Part1.D10_PWM/SS, Part4.1, J2.pulse, J6.pin1
  N16: Part1.D11_PWM/MOSI, Part4.2, J3.pulse, J7.pin1
  N17: Part1.D12/MISO, Part4.3, J4.pulse, J8.pin1
  N18: Part1.D13/SCK, R5_220Ω_LED1.Pin_0
  N19: Part1.D0/RX, Q2.C, R3_1kΩ_INV1.Pin_0
  N20: Part1.D2, Part4.OE, R2.Pin_0
  N21: Part1.D3_PWM, Part3.TX2_HV
  3V3: Part1.3V3, Part3.LV, U11.3V3, S1.leg1
  N22: Part3.TX_LV, S_BUS_in.pin1, U10.S.BUS
  N23: Part3.TX_HV, R3_1kΩ_INV2.Pin_1
  N24: Q2.B, R3_1kΩ_INV2.Pin_0
  N25: LED_(BBB)1.anode, R5_220Ω_LED1.Pin_1
  N26: LED_(BBB)2.anode, R5_220Ω_LED2.Pin_0

notes:
  Power options:
  5V, 1A to barrel plug on BBB (positive in the middle of the barrel plug). 3rd line (Expansion header, PIN 5-6) will provide power if BBB is powered from the barrel plug.
  Power BBB via 3rd line (Expansion header, PIN 5-6), 5V +/- 0.25V. This is used on Hugin. 5V from RC receiver, PWM in, PWM out.
  Hugin
  3V3 GND
  5V GND
  Spare
  (
  3.3V
  5V
  S.BUS out

custom parts:
  BeagleBone Black: BeagleBone Black rev. A5B
  Mystery Part - 10 pins: A dummy, proxy, ersatz, stand-in part for whatever you want. With 10 pins on a 300mil inline pin header footprint.
  2.1mm DC Barrel Jack: 2.1mm DC Barrel Jack with Thru-Hole Connectors (breadboardable)
  FreeIMU: A dummy, proxy, ersatz, stand-in part for whatever you want. With 8 pins on a 100 mil inline pin header footprint.
  16-Channel 12-bit PCA9685 PWM/Servo Driver: The Adafruit 16-Channel 12-bit PWM/Servo Driver will drive up to 16 servos over I2C with only 2 pins. The on-board PCA9685 PWM controller will drive all 16 channels simultaneously with no additional processing overhead. What's more, you can chain up to 62 of them to control up to 992 servos - all with the same 2 pins
  Mystery Part - 8 pins: A dummy, proxy, ersatz, stand-in part for whatever you want. With 8 pins on a 100 mil inline pin header footprint.
